# Fritzing sketch DigitalPotentiometer-NodeMCU (saved by Fritzing 0.9.3b)
breadboards: 1

parts:
  U1 = NodeMCU V1.0
  MCP1 = Potentiometer [package="DIP (Dual Inline) [THT]"]
  LED1 = smd LED [color="Red (633nm)" package="1206 [SMD]"]

nets:
  N1: U1.D2, MCP1.CS
  N2: U1.3V3#5, MCP1.PA0, MCP1.Vdd, LED1.cathode
  N3: U1.D5, MCP1.SCK
  N4: U1.D7, MCP1.Si
  N5: U1.GND#16, MCP1.Vss, MCP1.PB0, LED1.anode
  N6: U1.A0, MCP1.PW0

custom parts:
  NodeMCU V1.0: ESP8266 based NodeMCU V1.0
  Potentiometer: Digital Potentiometer
